// Logisim project alu.circ as structural Verilog: 1 circuit, main circuit alu
module alu (
  input  [31:0] A,
  input  [31:0] B,
  input  [3:0] ALUSel,
  output [31:0] ALUResult
);

  wire bitselector_1_out, bitselector_2_out, comparator_1_lt, xor_1_out;
  wire [31:0] abs_out_a, abs_out_b, add0, and0, mul0, mulh0, mulhu0, multiplier_1_cout, multiplier_1_out,
       negator_1_out, negator_2_out, or0, sll0, slt0, sra0, srl0, sub0, xor0;
  wire [63:0] negator_3_out;

  Adder #(.width(32)) adder_1 (.a(A), .b(B), .out(add0));  // open: cin, cout
  Shifter #(.width(32)) shifter_1 (.in(A), .\dist (B[4:0]), .out(sll0));
  Comparator #(.width(32)) comparator_1 (.a(A), .b(B), .lt(comparator_1_lt));  // open: gt, eq
  assign slt0 = {{31{1'b0}}, comparator_1_lt};  // Bit_Extender bit_extender_1
  xor xor_1 (xor_1_out, A[31], B[31]);
  Negator #(.width(32)) negator_1 (.in(A), .out(negator_1_out));
  BitSelector #(.width(32)) bitselector_1 (.in(A), .out(bitselector_1_out), .sel({5{1'b1}}));
  Negator #(.width(32)) negator_2 (.in(B), .out(negator_2_out));
  BitSelector #(.width(32)) bitselector_2 (.in(B), .out(bitselector_2_out), .sel({5{1'b1}}));
  assign xor0 = A ^ B;  // XOR_Gate xor_2, 32 bits wide
  Multiplexer #(.enable("false"), .width(32)) multiplexer_1 (
    .in0(A), .in1(negator_1_out), .out(abs_out_a), .sel(bitselector_1_out));
  Multiplexer #(.enable("false"), .width(32)) multiplexer_2 (
    .in0(B), .in1(negator_2_out), .out(abs_out_b), .sel(bitselector_2_out));
  Shifter #(.shift("lr"), .width(32)) shifter_2 (.in(A), .\dist (B[4:0]), .out(srl0));
  assign or0 = A | B;  // OR_Gate or_1, 32 bits wide
  Multiplier #(.width(32)) multiplier_1 (
    .a(abs_out_a), .b(abs_out_b), .out(multiplier_1_out), .cout(multiplier_1_cout));  // open: cin
  assign and0 = A & B;  // AND_Gate and_1, 32 bits wide
  Multiplier #(.width(32)) multiplier_2 (.a(A), .b(B), .cout(mulhu0));  // open: out, cin
  Shifter #(.shift("ar"), .width(32)) shifter_3 (.in(A), .\dist (B[4:0]), .out(sra0));
  Multiplexer #(.enable("false"), .width(64)) multiplexer_3 (
    .in0({multiplier_1_cout, multiplier_1_out}), .in1(negator_3_out), .out({mulh0, mul0}), .sel(xor_1_out));
  Negator #(.width(64)) negator_3 (.in({multiplier_1_cout, multiplier_1_out}), .out(negator_3_out));
  Subtractor #(.width(32)) subtractor_1 (.a(A), .b(B), .out(sub0));  // open: bin, bout
  Multiplexer #(.enable("false"), .select(4), .width(32)) multiplexer_4 (
    .in0(add0), .in1(sll0), .in2(slt0), .in4(xor0), .in5(srl0), .in6(or0), .in7(and0), .in8(mul0),
    .in9(mulh0), .in11(mulhu0), .in12(sub0), .in13(sra0), .in15(B), .out(ALUResult), .sel(ALUSel));  // open: in3, in10, in14

  // Other names for the same wires on the sheet: abs_in_a[31:0] = A; abs_in_b[31:0] = B; bsel0[31:0] = B

  // Notes on the sheet:
  //   INPUTS to your circuit
  //   DON'T CHANGE THE LOCATIONS OF THE INPUTS AND OUTPUTS!
  //   OUTPUT from your circuit
endmodule
