// Logisim project control-logic.circ as structural Verilog: 1 circuit, main circuit control_logic
module control_logic (
  input  [31:0] Instruction,
  input  BrEq,
  input  BrLt,
  output PCSel,
  output RegWEn,
  output [2:0] ImmSel,
  output BrUn,
  output ASel,
  output BSel,
  output [3:0] ALUSel,
  output MemWEn,
  output [1:0] WBSel
);

  wire add, addi, and0, and_9_out, andi, auipc, B_type, beq, bge, bgeu, blt, bltu, bne, comparator_1_eq,
       comparator_2_eq, comparator_3_eq, comparator_4_eq, comparator_5_eq, comparator_6_eq, comparator_7_eq,
       comparator_8_eq, comparator_9_eq, comparator_10_eq, comparator_11_eq, comparator_12_eq,
       comparator_13_eq, comparator_14_eq, comparator_15_eq, decoder_2_out2, decoder_2_out3, decoder_3_out5,
       jal, lui, mul, mulh, mulhu, not_1_out, not_2_out, not_3_out, Op_0x03, Op_0x13, Op_0x23, Op_0x67, or0,
       or_1_out, ori, PCSel0, PCSel1, PCSel2, PCSel3, PCSel4, PCSel5, R_type, R_type0, R_type1, R_type2,
       R_type3, R_type4, R_type5, R_type6, R_type7, sll0, slli, slt, slti, sra0, srai, srl0, srli, sub, xor0,
       xori;
  wire [15:0] rom_1_data;

  Decoder #(.enable("false"), .select(5)) decoder_1 (
    .out0(Op_0x03), .out4(Op_0x13), .out5(auipc), .out8(Op_0x23), .out12(R_type), .out13(lui),
    .out24(B_type), .out25(Op_0x67), .out27(jal), .sel(Instruction[6:2]));  // open: out1, out2, out3, out6, out7, out9, out10, out11, out14, out15, out16, out17, out18, out19, out20, out21, out22, out23, out26, out28, out29, out30, out31
  ROM #(.addrWidth(6), .dataWidth(16)) rom_1 (.data(rom_1_data));  // open: addr
  assign PCSel = Op_0x13 ? 1'b0 : 1'bz;  // Controlled_Buffer controlled_buffer_1
  assign ALUSel = addi ? 4'b0000 : 4'bz;  // Controlled_Buffer controlled_buffer_2
  assign ALUSel = slli ? 4'b0001 : 4'bz;  // Controlled_Buffer controlled_buffer_3
  Decoder #(.select(3)) decoder_2 (
    .out0(beq), .out1(bne), .out2(decoder_2_out2), .out3(decoder_2_out3), .out4(blt), .out5(bge),
    .out6(bltu), .out7(bgeu), .sel(Instruction[14:12]), .en(B_type));
  assign BrUn = beq ? 1'b0 : 1'bz;  // Controlled_Buffer controlled_buffer_4
  assign BrUn = bne ? 1'b0 : 1'bz;  // Controlled_Buffer controlled_buffer_5
  not not_1 (not_1_out, BrEq);
  Decoder #(.select(3)) decoder_3 (
    .out0(addi), .out1(slli), .out2(slti), .out4(xori), .out5(decoder_3_out5), .out6(ori), .out7(andi),
    .sel(Instruction[14:12]), .en(Op_0x13));  // open: out3
  assign ASel = B_type ? 1'b0 : 1'bz;  // Controlled_Buffer controlled_buffer_6
  and and_1 (PCSel0, beq, BrEq);
  and and_2 (PCSel1, bne, not_1_out);
  assign ASel = Op_0x13 ? 1'b1 : 1'bz;  // Controlled_Buffer controlled_buffer_7
  assign BSel = B_type ? 1'b1 : 1'bz;  // Controlled_Buffer controlled_buffer_8
  assign BSel = Op_0x13 ? 1'b1 : 1'bz;  // Controlled_Buffer controlled_buffer_9
  assign ALUSel = slti ? 4'b0010 : 4'bz;  // Controlled_Buffer controlled_buffer_10
  assign ALUSel = xori ? 4'b0100 : 4'bz;  // Controlled_Buffer controlled_buffer_11
  assign BrUn = blt ? 1'b0 : 1'bz;  // Controlled_Buffer controlled_buffer_12
  Comparator #(.width(7)) comparator_1 (.a(Instruction[31:25]), .b({7{1'b0}}), .eq(comparator_1_eq));  // open: gt, lt
  Comparator #(.width(7)) comparator_2 (.a(Instruction[31:25]), .b(7'b0100000), .eq(comparator_2_eq));  // open: gt, lt
  assign ImmSel = B_type ? 3'b010 : 3'bz;  // Controlled_Buffer controlled_buffer_13
  and and_3 (PCSel2, blt, BrLt);
  assign BrUn = bge ? 1'b0 : 1'bz;  // Controlled_Buffer controlled_buffer_14
  and and_4 (PCSel3, bge, not_2_out);
  not not_2 (not_2_out, BrLt);
  and and_5 (srli, comparator_1_eq, decoder_3_out5);
  and and_6 (srai, comparator_2_eq, decoder_3_out5);
  assign ImmSel = Op_0x13 ? 3'b000 : 3'bz;  // Controlled_Buffer controlled_buffer_15
  assign ALUSel = srli ? 4'b0101 : 4'bz;  // Controlled_Buffer controlled_buffer_16
  assign ALUSel = srai ? 4'b1101 : 4'bz;  // Controlled_Buffer controlled_buffer_17
  or or_1 (or_1_out, PCSel0, PCSel1, PCSel2, PCSel3, PCSel4, PCSel5);
  assign RegWEn = B_type ? 1'b0 : 1'bz;  // Controlled_Buffer controlled_buffer_18
  assign WBSel = Op_0x13 ? 2'b01 : 2'bz;  // Controlled_Buffer controlled_buffer_19
  assign PCSel = B_type ? or_1_out : 1'bz;  // Controlled_Buffer controlled_buffer_20
  assign ALUSel = ori ? 4'b0110 : 4'bz;  // Controlled_Buffer controlled_buffer_21
  assign ALUSel = andi ? 4'b0111 : 4'bz;  // Controlled_Buffer controlled_buffer_22
  assign MemWEn = B_type ? 1'b0 : 1'bz;  // Controlled_Buffer controlled_buffer_23
  assign BrUn = bltu ? 1'b1 : 1'bz;  // Controlled_Buffer controlled_buffer_24
  assign BrUn = bgeu ? 1'b1 : 1'bz;  // Controlled_Buffer controlled_buffer_25
  not not_3 (not_3_out, BrLt);
  assign RegWEn = Op_0x13 ? 1'b1 : 1'bz;  // Controlled_Buffer controlled_buffer_26
  and and_7 (PCSel4, bltu, BrLt);
  and and_8 (PCSel5, bgeu, not_3_out);
  assign MemWEn = Op_0x13 ? 1'b0 : 1'bz;  // Controlled_Buffer controlled_buffer_27
  Comparator #(.width(3)) comparator_3 (.a(Instruction[14:12]), .b(3'b000), .eq(comparator_3_eq));  // open: gt, lt
  Decoder #(.select(3)) decoder_4 (
    .out0(R_type0), .out1(R_type1), .out2(R_type2), .out3(R_type3), .out4(R_type4), .out5(R_type5),
    .out6(R_type6), .out7(R_type7), .sel(Instruction[14:12]), .en(R_type));
  and and_9 (and_9_out, Op_0x67, comparator_3_eq);
  assign PCSel = Op_0x03 ? 1'b0 : 1'bz;  // Controlled_Buffer controlled_buffer_28
  assign PCSel = Op_0x23 ? 1'b0 : 1'bz;  // Controlled_Buffer controlled_buffer_29
  assign PCSel = jal ? 1'b1 : 1'bz;  // Controlled_Buffer controlled_buffer_30
  assign PCSel = and_9_out ? 1'b1 : 1'bz;  // Controlled_Buffer controlled_buffer_31
  assign PCSel = auipc ? 1'b0 : 1'bz;  // Controlled_Buffer controlled_buffer_32
  assign PCSel = lui ? 1'b0 : 1'bz;  // Controlled_Buffer controlled_buffer_33
  assign ASel = Op_0x03 ? 1'b1 : 1'bz;  // Controlled_Buffer controlled_buffer_34
  assign ASel = jal ? 1'b0 : 1'bz;  // Controlled_Buffer controlled_buffer_35
  assign ASel = and_9_out ? 1'b1 : 1'bz;  // Controlled_Buffer controlled_buffer_36
  assign ASel = auipc ? 1'b0 : 1'bz;  // Controlled_Buffer controlled_buffer_37
  assign BSel = lui ? 1'b1 : 1'bz;  // Controlled_Buffer controlled_buffer_38
  assign ASel = R_type ? 1'b1 : 1'bz;  // Controlled_Buffer controlled_buffer_39
  assign ASel = Op_0x23 ? 1'b1 : 1'bz;  // Controlled_Buffer controlled_buffer_40
  Comparator #(.width(7)) comparator_4 (.a(Instruction[31:25]), .b({7{1'b0}}), .eq(comparator_4_eq));  // open: gt, lt
  Comparator #(.width(7)) comparator_5 (.a(Instruction[31:25]), .b(7'b0100000), .eq(comparator_5_eq));  // open: gt, lt
  Comparator #(.width(7)) comparator_6 (.a(Instruction[31:25]), .b(7'b0000001), .eq(comparator_6_eq));  // open: gt, lt
  Comparator #(.width(7)) comparator_7 (.a(Instruction[31:25]), .b({7{1'b0}}), .eq(comparator_7_eq));  // open: gt, lt
  Comparator #(.width(7)) comparator_8 (.a(Instruction[31:25]), .b(7'b0000001), .eq(comparator_8_eq));  // open: gt, lt
  Comparator #(.width(7)) comparator_9 (.a(Instruction[31:25]), .b({7{1'b0}}), .eq(comparator_9_eq));  // open: gt, lt
  assign BSel = Op_0x03 ? 1'b1 : 1'bz;  // Controlled_Buffer controlled_buffer_41
  assign BSel = Op_0x23 ? 1'b1 : 1'bz;  // Controlled_Buffer controlled_buffer_42
  assign BSel = jal ? 1'b1 : 1'bz;  // Controlled_Buffer controlled_buffer_43
  assign BSel = and_9_out ? 1'b1 : 1'bz;  // Controlled_Buffer controlled_buffer_44
  assign BSel = auipc ? 1'b1 : 1'bz;  // Controlled_Buffer controlled_buffer_45
  assign ImmSel = lui ? 3'b011 : 3'bz;  // Controlled_Buffer controlled_buffer_46
  assign BSel = R_type ? 1'b0 : 1'bz;  // Controlled_Buffer controlled_buffer_47
  assign ALUSel = add ? 4'b0000 : 4'bz;  // Controlled_Buffer controlled_buffer_48
  and and_10 (add, comparator_4_eq, R_type0);
  assign ALUSel = sub ? 4'b1100 : 4'bz;  // Controlled_Buffer controlled_buffer_49
  and and_11 (sub, comparator_5_eq, R_type0);
  assign ALUSel = mul ? 4'b1000 : 4'bz;  // Controlled_Buffer controlled_buffer_50
  and and_12 (mul, comparator_6_eq, R_type0);
  assign ALUSel = sll0 ? 4'b0001 : 4'bz;  // Controlled_Buffer controlled_buffer_51
  and and_13 (sll0, comparator_7_eq, R_type1);
  assign ALUSel = mulh ? 4'b1001 : 4'bz;  // Controlled_Buffer controlled_buffer_52
  and and_14 (mulh, comparator_8_eq, R_type1);
  assign ALUSel = slt ? 4'b0010 : 4'bz;  // Controlled_Buffer controlled_buffer_53
  and and_15 (slt, comparator_9_eq, R_type2);
  assign ImmSel = Op_0x03 ? 3'b000 : 3'bz;  // Controlled_Buffer controlled_buffer_54
  assign ImmSel = Op_0x23 ? 3'b001 : 3'bz;  // Controlled_Buffer controlled_buffer_55
  assign ImmSel = jal ? 3'b100 : 3'bz;  // Controlled_Buffer controlled_buffer_56
  assign ImmSel = and_9_out ? 3'b000 : 3'bz;  // Controlled_Buffer controlled_buffer_57
  assign ImmSel = auipc ? 3'b011 : 3'bz;  // Controlled_Buffer controlled_buffer_58
  assign WBSel = lui ? 2'b01 : 2'bz;  // Controlled_Buffer controlled_buffer_59
  assign WBSel = R_type ? 2'b01 : 2'bz;  // Controlled_Buffer controlled_buffer_60
  assign WBSel = Op_0x03 ? 2'b10 : 2'bz;  // Controlled_Buffer controlled_buffer_61
  assign RegWEn = Op_0x23 ? 1'b0 : 1'bz;  // Controlled_Buffer controlled_buffer_62
  assign WBSel = jal ? 2'b00 : 2'bz;  // Controlled_Buffer controlled_buffer_63
  assign WBSel = and_9_out ? 2'b00 : 2'bz;  // Controlled_Buffer controlled_buffer_64
  assign WBSel = auipc ? 2'b01 : 2'bz;  // Controlled_Buffer controlled_buffer_65
  assign RegWEn = lui ? 1'b1 : 1'bz;  // Controlled_Buffer controlled_buffer_66
  assign RegWEn = R_type ? 1'b1 : 1'bz;  // Controlled_Buffer controlled_buffer_67
  Comparator #(.width(7)) comparator_10 (
    .a(Instruction[31:25]), .b(7'b0000001), .eq(comparator_10_eq));  // open: gt, lt
  Comparator #(.width(7)) comparator_11 (.a(Instruction[31:25]), .b({7{1'b0}}), .eq(comparator_11_eq));  // open: gt, lt
  Comparator #(.width(7)) comparator_12 (.a(Instruction[31:25]), .b({7{1'b0}}), .eq(comparator_12_eq));  // open: gt, lt
  Comparator #(.width(7)) comparator_13 (
    .a(Instruction[31:25]), .b(7'b0100000), .eq(comparator_13_eq));  // open: gt, lt
  Comparator #(.width(7)) comparator_14 (.a(Instruction[31:25]), .b({7{1'b0}}), .eq(comparator_14_eq));  // open: gt, lt
  Comparator #(.width(7)) comparator_15 (.a(Instruction[31:25]), .b({7{1'b0}}), .eq(comparator_15_eq));  // open: gt, lt
  assign RegWEn = Op_0x03 ? 1'b1 : 1'bz;  // Controlled_Buffer controlled_buffer_68
  assign RegWEn = jal ? 1'b1 : 1'bz;  // Controlled_Buffer controlled_buffer_69
  assign RegWEn = and_9_out ? 1'b1 : 1'bz;  // Controlled_Buffer controlled_buffer_70
  assign RegWEn = auipc ? 1'b1 : 1'bz;  // Controlled_Buffer controlled_buffer_71
  assign PCSel = R_type ? 1'b0 : 1'bz;  // Controlled_Buffer controlled_buffer_72
  assign ALUSel = mulhu ? 4'b1011 : 4'bz;  // Controlled_Buffer controlled_buffer_73
  and and_16 (mulhu, comparator_10_eq, R_type3);
  assign ALUSel = xor0 ? 4'b0100 : 4'bz;  // Controlled_Buffer controlled_buffer_74
  and and_17 (xor0, comparator_11_eq, R_type4);
  assign ALUSel = srl0 ? 4'b0101 : 4'bz;  // Controlled_Buffer controlled_buffer_75
  and and_18 (srl0, comparator_12_eq, R_type5);
  assign ALUSel = sra0 ? 4'b1101 : 4'bz;  // Controlled_Buffer controlled_buffer_76
  and and_19 (sra0, comparator_13_eq, R_type5);
  assign ALUSel = or0 ? 4'b0110 : 4'bz;  // Controlled_Buffer controlled_buffer_77
  and and_20 (or0, comparator_14_eq, R_type6);
  assign ALUSel = and0 ? 4'b0111 : 4'bz;  // Controlled_Buffer controlled_buffer_78
  and and_21 (and0, comparator_15_eq, R_type7);
  assign MemWEn = Op_0x23 ? 1'b1 : 1'bz;  // Controlled_Buffer controlled_buffer_79
  assign MemWEn = lui ? 1'b0 : 1'bz;  // Controlled_Buffer controlled_buffer_80
  assign MemWEn = Op_0x03 ? 1'b0 : 1'bz;  // Controlled_Buffer controlled_buffer_81
  assign MemWEn = jal ? 1'b0 : 1'bz;  // Controlled_Buffer controlled_buffer_82
  assign MemWEn = and_9_out ? 1'b0 : 1'bz;  // Controlled_Buffer controlled_buffer_83
  assign MemWEn = auipc ? 1'b0 : 1'bz;  // Controlled_Buffer controlled_buffer_84
  assign MemWEn = R_type ? 1'b0 : 1'bz;  // Controlled_Buffer controlled_buffer_85
  assign ALUSel = Op_0x23 ? 4'b0000 : 4'bz;  // Controlled_Buffer controlled_buffer_86
  assign ALUSel = lui ? 4'b1111 : 4'bz;  // Controlled_Buffer controlled_buffer_87
  assign ALUSel = Op_0x03 ? 4'b0000 : 4'bz;  // Controlled_Buffer controlled_buffer_88
  assign ALUSel = jal ? 4'b0000 : 4'bz;  // Controlled_Buffer controlled_buffer_89
  assign ALUSel = and_9_out ? 4'b0000 : 4'bz;  // Controlled_Buffer controlled_buffer_90
  assign ALUSel = auipc ? 4'b0000 : 4'bz;  // Controlled_Buffer controlled_buffer_91

  // Other names for the same wires on the sheet: opcode5[4:0] = Instruction[6:2]; funct3[2:0] = Instruction[14:12];
  //   funct7[6:0] = Instruction[31:25]

  // Notes on the sheet:
  //   INPUTS to your circuit
  //   Connect ROM Input here ->
  //   ROM FOR CONTROL LOGIC
  //   DON'T CHANGE THE LOCATIONS OF THE INPUTS AND OUTPUTS!
  //   This is only if you choose to do the ROM option
  //   CONNECT
  //   WIRE
  //   TO
  //   USE
  //   ROM
  //   OUTPUT from your circuit
  //   Reminder: If using ROM, use combinational logic for PCSel
endmodule
