// Logisim project cpu.circ as structural Verilog: 1 circuit, main circuit cpu
module cpu (
  input  clk,
  input  [31:0] Instruction,
  input  [31:0] MemReadData,
  output [31:0] MemAddress,
  output [31:0] ProgramCounter,
  output [31:0] ra,
  output [31:0] sp,
  output [31:0] t0,
  output [31:0] t1,
  output [31:0] t2,
  output [31:0] s0,
  output [31:0] s1,
  output [31:0] a0,
  output [3:0] MemWriteMask,
  output [31:0] MemWriteData
);

  wire ASel, BrEq, BrLt, BrUn, BSel, comparator_1_eq, comparator_2_eq, MemWEn, PCSel, PCSel_IF, RegWen;
  wire [1:0] WBSel;
  wire [2:0] funct3, ImmSel;
  wire [3:0] ALUSel;
  wire [4:0] imm12;
  wire [6:0] func7;
  wire [19:0] Instruction_t;
  wire [31:0] DataToReg, Immediate, multiplexer_1_out, multiplexer_2_out, multiplexer_4_out,
       multiplexer_5_out, PC_EX, PC_EXplus4, PCplus4, RegReadData1, RegReadData2, write_data;

  Adder #(.width(32)) adder_1 (.a(ProgramCounter), .b(32'h4), .out(PCplus4));  // open: cin, cout
  Register #(.width(32)) PC (.D(multiplexer_1_out), .clk(clk), .Q(ProgramCounter));  // open: en, clr
  Multiplexer #(.enable("false"), .width(32)) multiplexer_1 (
    .in0(PCplus4), .in1(MemAddress), .out(multiplexer_1_out), .sel(PCSel_IF));
  Comparator #(.width(1)) comparator_1 (.a(PCSel_IF), .b(1'b1), .eq(comparator_1_eq));  // open: gt, lt
  Multiplexer #(.enable("false"), .width(32)) multiplexer_2 (
    .in0(Instruction), .in1({32{1'b0}}), .out(multiplexer_2_out), .sel(comparator_1_eq));
  Register #(.width(32)) register_1 (.D(ProgramCounter), .clk(clk), .Q(PC_EX));  // open: en, clr
  Register #(.width(32)) register_2 (
    .D(multiplexer_2_out), .clk(clk), .Q({func7, imm12, Instruction_t[19:15], funct3, Instruction_t[11:0]}));  // open: en, clr
  Comparator #(.width(32)) comparator_2 (.a(ProgramCounter), .b({32{1'b0}}), .eq(comparator_2_eq));  // open: gt, lt
  Multiplexer #(.enable("false")) multiplexer_3 (.in0(PCSel), .in1(1'b0), .out(PCSel_IF), .sel(comparator_2_eq));
  Adder #(.width(32)) adder_2 (.a(PC_EX), .b(32'h4), .out(PC_EXplus4));  // open: cin, cout
  control_logic control_logic_1 (
    .PCSel(PCSel), .RegWEn(RegWen), .ImmSel(ImmSel), .BrUn(BrUn), .ASel(ASel), .BSel(BSel), .ALUSel(ALUSel),
    .MemWEn(MemWEn), .WBSel(WBSel),
    .Instruction({func7, imm12, Instruction_t[19:15], funct3, Instruction_t[11:0]}), .BrEq(BrEq), .BrLt(BrLt));
  regfile regfile_1 (
    .ReadReg1(Instruction_t[19:15]), .ReadReg2(imm12), .WriteReg(Instruction_t[11:7]),
    .RegWriteData(write_data), .RegWEn(RegWen), .clk(clk), .ra(ra), .sp(sp), .t0(t0), .t1(t1), .t2(t2),
    .s0(s0), .s1(s1), .a0(a0), .RegReadData1(RegReadData1), .RegReadData2(RegReadData2));
  imm_gen imm_gen_1 (
    .Instruction({func7, imm12, Instruction_t[19:15], funct3, Instruction_t[11:0]}), .ImmSel(ImmSel),
    .Immediate(Immediate));
  Multiplexer #(.enable("false"), .width(32)) multiplexer_4 (
    .in0(PC_EX), .in1(RegReadData1), .out(multiplexer_4_out), .sel(ASel));
  Multiplexer #(.enable("false"), .width(32)) multiplexer_5 (
    .in0(RegReadData2), .in1(Immediate), .out(multiplexer_5_out), .sel(BSel));
  alu alu_1 (.ALUResult(MemAddress), .A(multiplexer_4_out), .B(multiplexer_5_out), .ALUSel(ALUSel));
  branch_comp branch_comp_1 (.BrData1(RegReadData1), .BrData2(RegReadData2), .BrUn(BrUn), .BrEq(BrEq), .BrLt(BrLt));
  Multiplexer #(.enable("false"), .select(2), .width(32)) multiplexer_6 (
    .in0(PC_EXplus4), .in1(MemAddress), .in2(DataToReg), .out(write_data), .sel(WBSel));  // open: in3
  partial_store partial_store_1 (
    .Instruction({func7, imm12, Instruction_t[19:15], funct3, Instruction_t[11:0]}), .MemAddress(MemAddress),
    .DataFromReg(RegReadData2), .MemWEn(MemWEn), .MemWriteMask(MemWriteMask), .DataToMem(MemWriteData));
  partial_load partial_load_1 (
    .Instruction({func7, imm12, Instruction_t[19:15], funct3, Instruction_t[11:0]}), .MemAddress(MemAddress),
    .DataFromMem(MemReadData), .DataToReg(DataToReg));

  // Other names for the same wires on the sheet: alu_out[31:0] = MemAddress; Instruction_fetched[31:0] = Instruction;
  //   opcode[6:0] = Instruction_t[6:0]; rd[4:0] = Instruction_t[11:7];
  //   Instruction_t (some bits) = {func7, imm12, funct3}; rs1[4:0] = Instruction_t[19:15]; rs2[4:0] = imm12;
  //   imm12[11:5] = func7

  // Notes on the sheet:
  //   To IMEM
  //   IMEM (do **NOT** move this)
  //   From IMEM
  //   Inputs/Outputs for testing. Do **NOT** move these.
  //   To DMEM
  //   DMEM (do **NOT** move this)
  //   From DMEM
endmodule
