// Logisim project partial-load.circ as structural Verilog: 1 circuit, main circuit partial_load
module partial_load (
  input  [31:0] Instruction,
  input  [31:0] MemAddress,
  input  [31:0] DataFromMem,
  output [31:0] DataToReg
);

  wire [7:0] shifter_1_out;
  wire [15:8] shifter_1_out_2;
  wire [31:0] bit_extender_1_out, bit_extender_2_out;
  wire [31:16] shifter_1_out_3;

  Shifter #(.shift("lr"), .width(32)) shifter_1 (
    .in(DataFromMem), .\dist ({MemAddress[1:0], 3'b000}),
    .out({shifter_1_out_3, shifter_1_out_2, shifter_1_out}));
  assign bit_extender_1_out = {{24{shifter_1_out[7]}}, shifter_1_out};  // Bit_Extender bit_extender_1
  assign bit_extender_2_out = {{16{shifter_1_out_2[15]}}, {shifter_1_out_2, shifter_1_out}};  // Bit_Extender bit_extender_2
  Multiplexer #(.enable("false"), .select(2), .width(32)) multiplexer_1 (
    .in0(bit_extender_1_out), .in1(bit_extender_2_out),
    .in2({shifter_1_out_3, shifter_1_out_2, shifter_1_out}), .out(DataToReg), .sel(Instruction[13:12]));  // open: in3

  // Notes on the sheet:
  //   INPUTS to your circuit
  //   DON'T CHANGE THE LOCATIONS OF THE INPUTS AND OUTPUTS!
  //   OUTPUT from your circuit
endmodule
