// Logisim project partial-store.circ as structural Verilog: 1 circuit, main circuit partial_store
module partial_store (
  input  [31:0] Instruction,
  input  [31:0] MemAddress,
  input  [31:0] DataFromReg,
  input  MemWEn,
  output [3:0] MemWriteMask,
  output [31:0] DataToMem
);

  wire [3:0] decoder_1_out0, multiplexer_2_out, multiplexer_3_out;
  wire [4:0] multiplexer_1_out;
  wire [31:0] shifter_1_out, shifter_2_out, shifter_3_out;

  Multiplexer #(.enable("false"), .select(2), .width(5)) multiplexer_1 (
    .in0(5'b11000), .in1(5'b10000), .in2({5{1'b0}}), .out(multiplexer_1_out), .sel(Instruction[13:12]));  // open: in3
  Shifter #(.width(32)) shifter_1 (.in(DataFromReg), .\dist (multiplexer_1_out), .out(shifter_1_out));
  Shifter #(.shift("lr"), .width(32)) shifter_2 (.in(shifter_1_out), .\dist (multiplexer_1_out), .out(shifter_2_out));
  Decoder #(.enable("false"), .select(2)) decoder_1 (
    .out0(decoder_1_out0[0]), .out1(decoder_1_out0[1]), .out2(decoder_1_out0[2]), .out3(decoder_1_out0[3]),
    .sel(MemAddress[1:0]));
  Multiplexer #(.enable("false"), .select(2), .width(4)) multiplexer_2 (
    .in0(4'b0011), .in2(4'b1100), .out(multiplexer_2_out), .sel(MemAddress[1:0]));  // open: in1, in3
  Shifter #(.width(32)) shifter_3 (.in(shifter_2_out), .\dist ({MemAddress[1:0], 3'b000}), .out(shifter_3_out));
  Multiplexer #(.enable("false"), .select(2), .width(4)) multiplexer_3 (
    .in0(decoder_1_out0), .in1(multiplexer_2_out), .in2(4'b1111), .out(multiplexer_3_out),
    .sel(Instruction[13:12]));  // open: in3
  assign DataToMem = MemWEn ? shifter_3_out : 32'bz;  // Controlled_Buffer controlled_buffer_1
  Multiplexer #(.enable("false"), .width(4)) multiplexer_4 (
    .in0(4'b0000), .in1(multiplexer_3_out), .out(MemWriteMask), .sel(MemWEn));

  // Other names for the same wires on the sheet: funct3[1:0] = Instruction[13:12]

  // Notes on the sheet:
  //   INPUTS to your circuit
  //   DON'T CHANGE THE LOCATIONS OF THE INPUTS AND OUTPUTS!
  //   OUTPUT from your circuit
endmodule
