// Logisim project regfile.circ as structural Verilog: 1 circuit, main circuit regfile
module regfile (
  input  [4:0] ReadReg1,
  input  [4:0] ReadReg2,
  input  [4:0] WriteReg,
  input  [31:0] RegWriteData,
  input  RegWEn,
  input  clk,
  output [31:0] ra,
  output [31:0] sp,
  output [31:0] t0,
  output [31:0] t1,
  output [31:0] t2,
  output [31:0] s0,
  output [31:0] s1,
  output [31:0] a0,
  output [31:0] RegReadData1,
  output [31:0] RegReadData2
);

  wire RegWEn0, RegWEn0in, RegWEn1, RegWEn1in, RegWEn2, RegWEn2in, RegWEn3, RegWEn3in, RegWEn4, RegWEn4in,
       RegWEn5, RegWEn5in, RegWEn6, RegWEn6in, RegWEn7, RegWEn7in, RegWEn8, RegWEn8in, RegWEn9, RegWEn9in,
       RegWEn10, RegWEn10in, RegWEn11, RegWEn11in, RegWEn12, RegWEn12in, RegWEn13, RegWEn13in, RegWEn14,
       RegWEn14in, RegWEn15, RegWEn15in, RegWEn16, RegWEn16in, RegWEn17, RegWEn17in, RegWEn18, RegWEn18in,
       RegWEn19, RegWEn19in, RegWEn20, RegWEn20in, RegWEn21, RegWEn21in, RegWEn22, RegWEn22in, RegWEn23,
       RegWEn23in, RegWEn24, RegWEn24in, RegWEn25, RegWEn25in, RegWEn26, RegWEn26in, RegWEn27, RegWEn27in,
       RegWEn28, RegWEn28in, RegWEn29, RegWEn29in, RegWEn30, RegWEn30in, RegWEn31, RegWEn31in;
  wire [31:0] w_x0, w_x1, w_x2, w_x3, w_x4, w_x5, w_x6, w_x7, w_x8, w_x9, w_x10, w_x11, w_x12, w_x13, w_x14,
       w_x15, w_x16, w_x17, w_x18, w_x19, w_x20, w_x21, w_x22, w_x23, w_x24, w_x25, w_x26, w_x27, w_x28,
       w_x29, w_x30, w_x31, x3, x4, x11, x12, x13, x14, x15, x16, x17, x18, x19, x20, x21, x22, x23, x24,
       x25, x26, x27, x28, x29, x30, x31;

  Register #(.width(32)) register_1 (.D(w_x1), .en(RegWEn1), .clk(clk), .Q(ra));  // open: clr
  Register #(.width(32)) register_2 (.D(w_x2), .en(RegWEn2), .clk(clk), .Q(sp));  // open: clr
  Register #(.width(32)) register_3 (.D(w_x3), .en(RegWEn3), .clk(clk), .Q(x3));  // open: clr
  Register #(.width(32)) register_4 (.D(w_x4), .en(RegWEn4), .clk(clk), .Q(x4));  // open: clr
  Register #(.width(32)) register_5 (.D(w_x5), .en(RegWEn5), .clk(clk), .Q(t0));  // open: clr
  Register #(.width(32)) register_6 (.D(w_x6), .en(RegWEn6), .clk(clk), .Q(t1));  // open: clr
  Register #(.width(32)) register_7 (.D(w_x7), .en(RegWEn7), .clk(clk), .Q(t2));  // open: clr
  Decoder #(.enable("false"), .select(5)) decoder_1 (
    .out0(RegWEn0in), .out1(RegWEn1in), .out2(RegWEn2in), .out3(RegWEn3in), .out4(RegWEn4in),
    .out5(RegWEn5in), .out6(RegWEn6in), .out7(RegWEn7in), .out8(RegWEn8in), .out9(RegWEn9in),
    .out10(RegWEn10in), .out11(RegWEn11in), .out12(RegWEn12in), .out13(RegWEn13in), .out14(RegWEn14in),
    .out15(RegWEn15in), .out16(RegWEn16in), .out17(RegWEn17in), .out18(RegWEn18in), .out19(RegWEn19in),
    .out20(RegWEn20in), .out21(RegWEn21in), .out22(RegWEn22in), .out23(RegWEn23in), .out24(RegWEn24in),
    .out25(RegWEn25in), .out26(RegWEn26in), .out27(RegWEn27in), .out28(RegWEn28in), .out29(RegWEn29in),
    .out30(RegWEn30in), .out31(RegWEn31in), .sel(WriteReg));
  Register #(.width(32)) register_8 (.D(w_x8), .en(RegWEn8), .clk(clk), .Q(s0));  // open: clr
  Register #(.width(32)) register_9 (.D(w_x9), .en(RegWEn9), .clk(clk), .Q(s1));  // open: clr
  Register #(.width(32)) register_10 (.D(w_x10), .en(RegWEn10), .clk(clk), .Q(a0));  // open: clr
  Register #(.width(32)) register_11 (.D(w_x11), .en(RegWEn11), .clk(clk), .Q(x11));  // open: clr
  Register #(.width(32)) register_12 (.D(w_x12), .en(RegWEn12), .clk(clk), .Q(x12));  // open: clr
  Register #(.width(32)) register_13 (.D(w_x13), .en(RegWEn13), .clk(clk), .Q(x13));  // open: clr
  Register #(.width(32)) register_14 (.D(w_x14), .en(RegWEn14), .clk(clk), .Q(x14));  // open: clr
  Register #(.width(32)) register_15 (.D(w_x15), .en(RegWEn15), .clk(clk), .Q(x15));  // open: clr
  Register #(.width(32)) register_16 (.D(w_x16), .en(RegWEn16), .clk(clk), .Q(x16));  // open: clr
  Register #(.width(32)) register_17 (.D(w_x17), .en(RegWEn17), .clk(clk), .Q(x17));  // open: clr
  Register #(.width(32)) register_18 (.D(w_x18), .en(RegWEn18), .clk(clk), .Q(x18));  // open: clr
  Register #(.width(32)) register_19 (.D(w_x19), .en(RegWEn19), .clk(clk), .Q(x19));  // open: clr
  Register #(.width(32)) register_20 (.D(w_x20), .en(RegWEn20), .clk(clk), .Q(x20));  // open: clr
  Register #(.width(32)) register_21 (.D(w_x21), .en(RegWEn21), .clk(clk), .Q(x21));  // open: clr
  Register #(.width(32)) register_22 (.D(w_x22), .en(RegWEn22), .clk(clk), .Q(x22));  // open: clr
  Register #(.width(32)) register_23 (.D(w_x23), .en(RegWEn23), .clk(clk), .Q(x23));  // open: clr
  Demultiplexer #(.enable("false"), .select(5), .width(32)) demultiplexer_1 (
    .out0(w_x0), .out1(w_x1), .out2(w_x2), .out3(w_x3), .out4(w_x4), .out5(w_x5), .out6(w_x6), .out7(w_x7),
    .out8(w_x8), .out9(w_x9), .out10(w_x10), .out11(w_x11), .out12(w_x12), .out13(w_x13), .out14(w_x14),
    .out15(w_x15), .out16(w_x16), .out17(w_x17), .out18(w_x18), .out19(w_x19), .out20(w_x20), .out21(w_x21),
    .out22(w_x22), .out23(w_x23), .out24(w_x24), .out25(w_x25), .out26(w_x26), .out27(w_x27), .out28(w_x28),
    .out29(w_x29), .out30(w_x30), .out31(w_x31), .in(RegWriteData), .sel(WriteReg));
  Register #(.width(32)) register_24 (.D(w_x24), .en(RegWEn24), .clk(clk), .Q(x24));  // open: clr
  Register #(.width(32)) register_25 (.D(w_x25), .en(RegWEn25), .clk(clk), .Q(x25));  // open: clr
  Register #(.width(32)) register_26 (.D(w_x26), .en(RegWEn26), .clk(clk), .Q(x26));  // open: clr
  Register #(.width(32)) register_27 (.D(w_x27), .en(RegWEn27), .clk(clk), .Q(x27));  // open: clr
  Register #(.width(32)) register_28 (.D(w_x28), .en(RegWEn28), .clk(clk), .Q(x28));  // open: clr
  Register #(.width(32)) register_29 (.D(w_x29), .en(RegWEn29), .clk(clk), .Q(x29));  // open: clr
  Register #(.width(32)) register_30 (.D(w_x30), .en(RegWEn30), .clk(clk), .Q(x30));  // open: clr
  Register #(.width(32)) register_31 (.D(w_x31), .en(RegWEn31), .clk(clk), .Q(x31));  // open: clr
  Multiplexer #(.enable("false"), .select(5), .width(32)) multiplexer_1 (
    .in0({32{1'b0}}), .in1(ra), .in2(sp), .in3(x3), .in4(x4), .in5(t0), .in6(t1), .in7(t2), .in8(s0),
    .in9(s1), .in10(a0), .in11(x11), .in12(x12), .in13(x13), .in14(x14), .in15(x15), .in16(x16), .in17(x17),
    .in18(x18), .in19(x19), .in20(x20), .in21(x21), .in22(x22), .in23(x23), .in24(x24), .in25(x25),
    .in26(x26), .in27(x27), .in28(x28), .in29(x29), .in30(x30), .in31(x31), .out(RegReadData1), .sel(ReadReg1));
  and and_1 (RegWEn0, RegWEn0in, RegWEn);
  and and_2 (RegWEn1, RegWEn1in, RegWEn);
  and and_3 (RegWEn2, RegWEn2in, RegWEn);
  and and_4 (RegWEn3, RegWEn3in, RegWEn);
  and and_5 (RegWEn4, RegWEn4in, RegWEn);
  and and_6 (RegWEn5, RegWEn5in, RegWEn);
  and and_7 (RegWEn6, RegWEn6in, RegWEn);
  and and_8 (RegWEn7, RegWEn7in, RegWEn);
  and and_9 (RegWEn8, RegWEn8in, RegWEn);
  and and_10 (RegWEn9, RegWEn9in, RegWEn);
  and and_11 (RegWEn10, RegWEn10in, RegWEn);
  and and_12 (RegWEn11, RegWEn11in, RegWEn);
  and and_13 (RegWEn12, RegWEn12in, RegWEn);
  and and_14 (RegWEn13, RegWEn13in, RegWEn);
  and and_15 (RegWEn14, RegWEn14in, RegWEn);
  and and_16 (RegWEn15, RegWEn15in, RegWEn);
  Multiplexer #(.enable("false"), .select(5), .width(32)) multiplexer_2 (
    .in0({32{1'b0}}), .in1(ra), .in2(sp), .in3(x3), .in4(x4), .in5(t0), .in6(t1), .in7(t2), .in8(s0),
    .in9(s1), .in10(a0), .in11(x11), .in12(x12), .in13(x13), .in14(x14), .in15(x15), .in16(x16), .in17(x17),
    .in18(x18), .in19(x19), .in20(x20), .in21(x21), .in22(x22), .in23(x23), .in24(x24), .in25(x25),
    .in26(x26), .in27(x27), .in28(x28), .in29(x29), .in30(x30), .in31(x31), .out(RegReadData2), .sel(ReadReg2));
  and and_17 (RegWEn16, RegWEn16in, RegWEn);
  and and_18 (RegWEn17, RegWEn17in, RegWEn);
  and and_19 (RegWEn18, RegWEn18in, RegWEn);
  and and_20 (RegWEn19, RegWEn19in, RegWEn);
  and and_21 (RegWEn20, RegWEn20in, RegWEn);
  and and_22 (RegWEn21, RegWEn21in, RegWEn);
  and and_23 (RegWEn22, RegWEn22in, RegWEn);
  and and_24 (RegWEn23, RegWEn23in, RegWEn);
  and and_25 (RegWEn24, RegWEn24in, RegWEn);
  and and_26 (RegWEn25, RegWEn25in, RegWEn);
  and and_27 (RegWEn26, RegWEn26in, RegWEn);
  and and_28 (RegWEn27, RegWEn27in, RegWEn);
  and and_29 (RegWEn28, RegWEn28in, RegWEn);
  and and_30 (RegWEn29, RegWEn29in, RegWEn);
  and and_31 (RegWEn30, RegWEn30in, RegWEn);
  and and_32 (RegWEn31, RegWEn31in, RegWEn);

  // Other names for the same wires on the sheet: x1[31:0] = ra; x2[31:0] = sp; x5[31:0] = t0; x6[31:0] = t1;
  //   x7[31:0] = t2; x8[31:0] = s0; x9[31:0] = s1; x10[31:0] = a0

  // Notes on the sheet:
  //   INPUTS to your circuit
  //   DON'T CHANGE THE LOCATIONS OF THE INPUTS AND OUTPUTS!
  //   These are DEBUG/TEST outputs from your circuit.
  //   OUTPUTS from your circuit
endmodule
